# Fritzing sketch MQTT_ESP8266 (saved by Fritzing 0.9.3b)
breadboards: 1

parts:
  WeMos_D1_Mini1 = WeMos D1 Mini
  WeMos_D1_Mini2 = WeMos D1 Mini
  LED1 = LED - 5mm [color="Red (633nm)" package="5 mm [THT]"]
  R1 = Resistor [tolerance=±5% resistance=330 package=THT]
  S1 = Pushbutton [package="[THT]"]
  R2 = Resistor [tolerance=±5% resistance=10k package=THT]
  LED2 = LED - 5mm [color="Red (633nm)" package="5 mm [THT]"]
  R3 = Resistor [tolerance=±5% resistance=330 package=THT]
  S2 = Pushbutton [package="[THT]"]
  R4 = Resistor [tolerance=±5% resistance=10k package=THT]

nets:
  3.3V: WeMos_D1_Mini1.3V3, WeMos_D1_Mini2.3V3, R2.Pin_1, R4.Pin_0
  5V: WeMos_D1_Mini1.5V, WeMos_D1_Mini2.5V
  LED 1: WeMos_D1_Mini1.D1, R1.Pin_1
  BUTTON 1: WeMos_D1_Mini1.D2, S1.Pin_3, S1.Pin_4, R2.Pin_0
  GND: WeMos_D1_Mini1.G, WeMos_D1_Mini2.G, LED1.cathode, S1.Pin_1, S1.Pin_2, LED2.cathode, S2.Pin_3, S2.Pin_4
  LED 2: WeMos_D1_Mini2.D6, R3.Pin_1
  BUTTON 2: WeMos_D1_Mini2.D7, S2.Pin_1, S2.Pin_2, R4.Pin_1
  N1: LED1.anode, R1.Pin_0
  N2: LED2.anode, R3.Pin_0

notes:
  ESP8266 TUTORIAL, GIAO TIẾP GIỮA CÁC ESP8266 VỚI MQTT     THỰC HIỆN: THI MINH NHỰT, V1.0.0
